// Logisim project CPU.circ as structural Verilog: 1 circuit, main circuit cpu
// RegSegment
module cpu (
);

  wire and_2_out, and_7_out, and_8_out, and_23_out, and_24_out, and_25_out, and_26_out, and_27_out,
       and_28_out, and_29_out, and_30_out, and_36_out, and_37_out, and_38_out, and_39_out, and_40_out,
       and_41_out, and_42_out, and_43_out, and_45_out, and_46_out, and_51_out, clk, demultiplexer_1_out3,
       demultiplexer_2_out1, demultiplexer_2_out2, demultiplexer_2_out3, demultiplexer_2_out4,
       demultiplexer_2_out5, demultiplexer_2_out6, demultiplexer_2_out7, demultiplexer_2_out8,
       demultiplexer_2_out9, demultiplexer_2_out10, demultiplexer_2_out11, demultiplexer_2_out12,
       FLAGS_write, FLAGS_write_cmp, IC_editIntFlag, IC_interruptCLR, IC_intWasTrig, InstructionCache_write,
       interrupt_det_1_out_3, interrupt_det_2_out_3, InterruptMask_has1, InterruptMask_has2, JMP_enable,
       loadToRAM, main_1_out_3, main_2_out_3, main_3_out_3, main_4_out_3, main_5_out_3, main_6_out_3,
       main_7_out_3, main_8_out_3, main_9_out_3, main_10_out_3, main_11_out_3, main_12_out_3, main_13_out_3,
       main_14_out_3, main_15_out_3, main_16_out_3, main_17_out_3, main_18_out_3, main_19_out_3,
       main_24_out_3, main_25_out_3, main_26_out_3, main_27_out_3, main_28_out_3, main_29_out_3,
       main_30_out_3, main_31_out_3, main_32_out_3, main_33_out_3, main_34_out_3, main_35_out_3,
       main_36_out_3, main_37_out_3, main_38_out_3, main_39_out_3, main_40_out_3, main_41_out_3,
       main_42_out_3, main_43_out_3, main_44_out_3, main_45_out_3, main_46_out_3, main_47_out_3,
       main_48_out_3, main_49_out_3, main_50_out_3, main_51_out_3, main_52_out_3, main_53_out_3,
       main_54_out_3, main_55_out_3, main_56_out_3, main_57_out_3, main_58_out_3, main_59_out_3,
       main_60_out_3, main_61_out_3, main_64_out_3, main_65_out_3, main_66_out_3, main_67_out_3,
       main_68_out_3, main_69_out_3, main_70_out_3, main_71_out_3, main_72_out_3, main_73_out_3,
       main_74_out_3, main_75_out_3, main_76_out_3, main_77_out_3, main_78_out_3, main_79_out_3,
       main_80_out_3, main_81_out_3, main_82_out_3, main_83_out_3, main_84_out_3, main_85_out_3,
       main_86_out_3, main_87_out_3, main_88_out_3, main_89_out_3, main_90_out_3, main_91_out_3,
       main_92_out_3, main_93_out_3, main_94_out_3, main_95_out_3, main_96_out_3, main_97_out_3,
       main_98_out_3, main_99_out_3, main_103_out_3, main_104_out_3, main_105_out_3, main_108_out_3,
       main_109_out_3, main_110_out_3, main_111_out_3, main_112_out_3, main_113_out_3, main_114_out_3,
       main_115_out_3, main_116_out_3, main_117_out_3, main_118_out_3, main_119_out_3, main_120_out_3,
       main_121_out_3, main_122_out_3, main_123_out_3, main_125_out_3, main_127_out_3, main_128_out_3,
       mem_wrt, not_1_out, not_2_out, not_3_out, not_4_out, not_7_out, not_8_out, not_9_out, not_10_out,
       not_11_out, not_14_out, not_15_out, not_16_out, not_17_out, not_18_out, not_19_out, not_20_out,
       not_21_out, not_22_out, not_23_out, Operand1Cache_write, or_1_out, or_3_out, or_10_out, or_11_out,
       or_12_out, or_13_out, or_14_out, or_17_out, or_18_out, or_19_out, or_20_out, or_21_out, or_22_out,
       or_24_out, or_26_out, or_27_out, or_29_out, or_30_out, or_32_out, or_33_out, or_34_out, or_35_out,
       or_36_out, or_37_out, or_38_out, or_39_out, or_40_out, or_41_out, or_42_out, or_43_out, or_45_out,
       or_46_out, or_49_out, or_50_out, or_52_out, or_54_out, or_55_out, or_56_out, priority_encoder_1_p1,
       priority_encoder_2_gs, R0_write, R1_write, R2_write, R3_write, R4_write, R5_write, R6_write, R7_write,
       ram_wrt, Reading_op2, Registers_allbits, Registers_highbits, Registers_highbits_req1,
       Registers_highbits_req2, Rseg_write, rst, Rtemp_loadFromRAM, Rtemp_loadFromREG, segment_enable,
       undriven;
  wire [1:0] ALU_cmp_out2, comparator_1_gt, counter_2_q, Rseg_out2, Rsel_out2;
  wire [3:0] ALU_select_in4, FLAGS_in4, FLAGS_out4, joystick_1_x, joystick_1_y, joystick_2_x, joystick_2_y;
  wire [6:0] and_34_out, and_35_out;
  wire [7:0] ALU_enable_AS8, ALU_out8HIGH, ALU_out8LOW, and_1_out, and_5_out, and_6_out, and_9_out,
       and_11_out, and_14_out, and_15_out, and_19_out, and_20_out, and_21_out, and_22_out, and_31_out,
       and_32_out, bit_extender_2_out, bit_extender_3_out, bit_extender_4_out, bit_extender_5_out,
       bit_extender_6_out, bit_extender_7_out, bit_extender_11_out, clk_inv_as8, controlled_buffer_5_out,
       IC_intNum_out8, InstructionCache_input8, InstructionCache_out8, InstructionCache_out8LOCK1,
       InstructionCache_out8SAFE, InterruptMasks_q, loadToMem_AS8, not_5_out, not_12_out, not_13_out,
       Operand1Cache_out8, Operand1Cache_out8LOCK1, or_4_out, or_5_out, or_6_out, or_44_out, or_44_out_2,
       ram_1_data, ram_2_data, ram_addr_in8, ram_read_out8, ram_write_in8, Reading_op2_ext8,
       Register_write_in8, Register_write_in_upper8, registerReadFromOp2_AS8, RegisterSelect_read_in8,
       RegisterSelect_read_out8HIGH, RegisterSelect_read_out8LOW, RegisterSelect_write_in8,
       Rsel_ctrl_lowerEnable, Rsel_ctrl_upperEnable, Rtemp_loadFromRAM_AS8, Rtemp_loadFromREG_AS8,
       Rtemp_loadFromSEG_AS8, segment_enable_AS8, undriven_2, undriven_3, undriven_4, undriven_5, undriven_6,
       undriven_7, undriven_8, undriven_9, undriven_10, undriven_11, undriven_12, undriven_13, undriven_14,
       undriven_15, undriven_16, undriven_17;
  wire [7:2] InterruptMask_out8, Operand1Cache_out8SAFE, Rseg_out8;
  wire [9:0] counter_1_q, JMP_addr;
  wire [9:8] ram_addr_in10;
  wire [15:0] adder_1_out, ALU_inputA_in16, ALU_inputB_in16, and_47_out, and_48_out, bit_extender_9_out,
       controlled_buffer_46_out, divider_1_out, multiplier_1_out, or_25_out, R0_out16, R1_out16, R2_out16,
       R3_out16, R4_out16, R5_out16, R6_out16, R7_out16, Rt16_input16, Rt16_out16, shifter_1_out,
       shifter_2_out, shifter_3_out, shifter_4_out, subtractor_1_out, xor_1_out;
  wire [15:8] registerReadFromOp2_AS16;

  Clock clock_1 (.out(clk));
  DipSwitch #(.number(2)) dipswitch_1 (.sw2(mem_wrt));  // open: sw1
  Button button_1 (.out(rst));
  Counter #(.max('h3ff), .width(10)) counter_1 (
    .load(JMP_enable), .D(JMP_addr), .Q(counter_1_q), .up(1'b1), .clk(clk), .clr(rst));  // open: count, carry
  not not_1 (not_1_out, mem_wrt);
  RAM #(.addrWidth(10), .databus("bidir"), .trigger("high")) ram_1 (
    .addr(counter_1_q), .we(mem_wrt), .oe(not_1_out), .clk(undriven), .data(ram_1_data));
  RAM #(.addrWidth(10), .databus("bidir"), .trigger("high")) ram_2 (
    .addr({ram_addr_in10, ram_addr_in8}), .we(ram_wrt), .oe(not_2_out), .data(ram_2_data));
  not not_2 (not_2_out, ram_wrt);
  not not_3 (not_3_out, mem_wrt);
  assign InstructionCache_input8 = not_3_out ? ram_1_data : 8'bz;  // Controlled_Buffer controlled_buffer_1
  Pull_Resistor pull_resistor_1 (.node(InstructionCache_input8));
  Counter #(.max('h3), .width(2)) counter_2 (
    .Q(counter_2_q), .up(1'b1), .clk(clk), .clr(or_1_out));  // open: load, D, count, carry
  assign Reading_op2_ext8 = {{7{Reading_op2}}, Reading_op2};  // Bit_Extender bit_extender_1
  assign bit_extender_2_out = {{7{Operand1Cache_write}}, Operand1Cache_write};  // Bit_Extender bit_extender_2
  assign and_1_out = bit_extender_2_out & Operand1Cache_out8;  // AND_Gate and_1, 8 bits wide
  assign ram_1_data = mem_wrt ? undriven_2 : 8'bz;  // Controlled_Buffer controlled_buffer_2
  Demultiplexer #(.select(2)) demultiplexer_1 (
    .out0(InstructionCache_write), .out1(Operand1Cache_write), .out2(Reading_op2),
    .out3(demultiplexer_1_out3), .in(1'b1), .sel(counter_2_q));
  and and_2 (and_2_out, counter_2_q[0], counter_2_q[1]);
  or or_1 (or_1_out, and_2_out, rst);
  assign JMP_addr[9:2] = InstructionCache_input8 & Reading_op2_ext8;  // AND_Gate and_3, 8 bits wide
  assign ram_addr_in8 = and_1_out | JMP_addr[9:2];  // OR_Gate or_2, 8 bits wide
  Button button_2 (.out(IC_interruptCLR));
  // DipSwitch dipswitch_2: pin names not known; wires that end beside it: demultiplexer_1_out3
  assign bit_extender_3_out = {{7{Operand1Cache_write}}, Operand1Cache_write};  // Bit_Extender bit_extender_3
  assign ram_2_data = ram_wrt ? ram_write_in8 : 8'bz;  // Controlled_Buffer controlled_buffer_3
  not not_4 (not_4_out, ram_wrt);
  assign ram_read_out8 = not_4_out ? ram_2_data : 8'bz;  // Controlled_Buffer controlled_buffer_4
  assign bit_extender_4_out = {{7{Registers_highbits}}, Registers_highbits};  // Bit_Extender bit_extender_4
  Joystick joystick_1 (.x(joystick_1_x), .y(joystick_1_y));
  Joystick joystick_2 (.x(joystick_2_x), .y(joystick_2_y));
  assign InstructionCache_out8LOCK1 = bit_extender_3_out & InstructionCache_out8;  // AND_Gate and_4, 8 bits wide
  or or_3 (or_3_out, Rtemp_loadFromRAM, segment_enable);
  assign and_5_out = RegisterSelect_read_out8HIGH & bit_extender_4_out;  // AND_Gate and_5, 8 bits wide
  assign not_5_out = ~bit_extender_4_out;  // NOT_Gate not_5, 8 bits wide
  assign and_6_out = not_5_out & RegisterSelect_read_out8LOW;  // AND_Gate and_6, 8 bits wide
  assign bit_extender_5_out = {{7{or_3_out}}, or_3_out};  // Bit_Extender bit_extender_5
  assign or_4_out = and_5_out | and_6_out;  // OR_Gate or_4, 8 bits wide
  interrupt_det interrupt_det_1 (
    .in_1({joystick_1_y, joystick_1_x}), .rst(IC_interruptCLR), .out_3(interrupt_det_1_out_3));
  and and_7 (and_7_out, interrupt_det_1_out_3, InterruptMask_has1, priority_encoder_1_p1);
  assign controlled_buffer_5_out = and_7_out ? 8'h1 : 8'bz;  // Controlled_Buffer controlled_buffer_5
  interrupt_det interrupt_det_2 (
    .in_1({joystick_2_y, joystick_2_x}), .rst(IC_interruptCLR), .out_3(interrupt_det_2_out_3));
  and and_8 (and_8_out, interrupt_det_2_out_3, InterruptMask_has2, priority_encoder_1_p1);
  assign controlled_buffer_5_out = and_8_out ? 8'h2 : 8'bz;  // Controlled_Buffer controlled_buffer_6
  // LedBar #(.inputtype("row")) ledbar_1: pin names not known; wires that end beside it: ram_write_in8
  assign and_9_out = bit_extender_5_out & ram_read_out8;  // AND_Gate and_9, 8 bits wide
  assign Rt16_input16[15:8] = Rtemp_loadFromREG_AS8 & or_4_out;  // AND_Gate and_10, 8 bits wide
  assign or_5_out = bit_extender_5_out | Rtemp_loadFromREG_AS8 | Rtemp_loadFromSEG_AS8;  // OR_Gate or_5, 8 bits wide
  assign and_11_out = Rtemp_loadFromSEG_AS8 & {Rseg_out8, Rseg_out2};  // AND_Gate and_11, 8 bits wide
  // Priority_Encoder priority_encoder_1: pin names not known; wires that end beside it: priority_encoder_1_p1, 1'b1
  // LedBar #(.inputtype("row")) ledbar_2: pin names not known; wires that end beside it: InstructionCache_out8SAFE
  // LedBar #(.inputtype("row")) ledbar_3: pin names not known; wires that end beside it: {Operand1Cache_out8SAFE, JMP_addr[1:0]}
  // LedBar #(.inputtype("row")) ledbar_4: pin names not known; wires that end beside it: JMP_addr[9:2]
  // LedBar #(.inputtype("row")) ledbar_5: pin names not known; wires that end beside it: Operand1Cache_out8LOCK1
  assign bit_extender_6_out = {{7{Operand1Cache_write}}, Operand1Cache_write};  // Bit_Extender bit_extender_6
  Priority_Encoder priority_encoder_2 (
    .in0(controlled_buffer_5_out[0]), .in1(controlled_buffer_5_out[1]), .in2(controlled_buffer_5_out[2]),
    .in3(controlled_buffer_5_out[3]), .in4(controlled_buffer_5_out[4]), .in5(controlled_buffer_5_out[5]),
    .in6(controlled_buffer_5_out[6]), .in7(controlled_buffer_5_out[7]), .en_in(1'b1),
    .gs(priority_encoder_2_gs));  // open: out, en_out
  Register register_1 (
    .D(controlled_buffer_5_out), .en(1'b1), .Q(IC_intNum_out8), .clk(priority_encoder_2_gs),
    .clr(IC_interruptCLR));
  assign Operand1Cache_out8LOCK1 = bit_extender_6_out & Operand1Cache_out8;  // AND_Gate and_12, 8 bits wide
  assign or_6_out = and_9_out | Rt16_input16[15:8] | and_11_out;  // OR_Gate or_6, 8 bits wide
  not not_6 (IC_intWasTrig, priority_encoder_1_p1);
  or or_7 (IC_editIntFlag, priority_encoder_2_gs, IC_interruptCLR);
  assign ram_addr_in10 = Rseg_out2 & {2{segment_enable}};  // AND_Gate and_13, 2 bits wide
  assign and_14_out = Rtemp_loadFromREG_AS8 & Operand1Cache_out8LOCK1;  // AND_Gate and_14, 8 bits wide
  assign and_15_out = registerReadFromOp2_AS8 & JMP_addr[9:2];  // AND_Gate and_15, 8 bits wide
  assign Rt16_input16[7:0] = or_5_out[0] ? or_6_out : 8'bz;  // Controlled_Buffer controlled_buffer_7
  assign Rt16_input16[7:0] = not_7_out ? Operand1Cache_out8LOCK1 : 8'bz;  // Controlled_Buffer controlled_buffer_8
  not not_7 (not_7_out, or_5_out[0]);
  // DipSwitch dipswitch_3: pin names not known
  // LedBar #(.inputtype("row")) ledbar_6: pin names not known; wires that end beside it: InstructionCache_out8LOCK1
  assign RegisterSelect_read_in8 = and_14_out | and_15_out;  // OR_Gate or_8, 8 bits wide
  Register #(.trigger("high")) InterruptMasks (
    .D(undriven_3), .en(1'b1), .Q(InterruptMasks_q), .clk(1'b1));  // open: clr
  assign bit_extender_7_out = {{7{1'b0}}, 1'b0};  // Bit_Extender bit_extender_7
  assign InstructionCache_out8SAFE = Reading_op2_ext8 & InstructionCache_out8;  // AND_Gate and_16, 8 bits wide
  assign {Operand1Cache_out8SAFE, JMP_addr[1:0]} = Reading_op2_ext8 & Operand1Cache_out8;  // AND_Gate and_17, 8 bits wide
  assign {InterruptMask_out8, InterruptMask_has2, InterruptMask_has1} = InterruptMasks_q & bit_extender_7_out;  // AND_Gate and_18, 8 bits wide
  or or_9 (Registers_highbits, Registers_highbits_req1, Registers_highbits_req2, 1'b0, 1'b0, 1'b0, 1'b0, 1'b0, 1'b0);
  or or_10 (or_10_out, Registers_highbits, Registers_allbits);
  not not_8 (not_8_out, or_10_out);
  not not_9 (not_9_out, or_10_out);
  not not_10 (not_10_out, or_10_out);
  not not_11 (not_11_out, or_10_out);
  assign and_19_out = ALU_enable_AS8 & ALU_out8LOW;  // AND_Gate and_19, 8 bits wide
  assign not_12_out = ~ALU_enable_AS8;  // NOT_Gate not_12, 8 bits wide
  assign and_20_out = not_12_out & ram_write_in8;  // AND_Gate and_20, 8 bits wide
  assign and_21_out = ALU_enable_AS8 & ALU_out8HIGH;  // AND_Gate and_21, 8 bits wide
  assign not_13_out = ~ALU_enable_AS8;  // NOT_Gate not_13, 8 bits wide
  assign and_22_out = not_13_out & ram_write_in8;  // AND_Gate and_22, 8 bits wide
  or or_11 (or_11_out, Registers_allbits, not_8_out);
  and and_23 (and_23_out, or_11_out, R0_write);
  and and_24 (and_24_out, R0_write, or_10_out);
  or or_12 (or_12_out, Registers_allbits, not_9_out);
  and and_25 (and_25_out, or_12_out, R1_write);
  and and_26 (and_26_out, R1_write, or_10_out);
  or or_13 (or_13_out, Registers_allbits, not_10_out);
  and and_27 (and_27_out, or_13_out, R2_write);
  and and_28 (and_28_out, R2_write, or_10_out);
  or or_14 (or_14_out, Registers_allbits, not_11_out);
  and and_29 (and_29_out, or_14_out, R3_write);
  and and_30 (and_30_out, R3_write, or_10_out);
  assign {RegisterSelect_read_out8HIGH, RegisterSelect_read_out8LOW} = RegisterSelect_read_in8[0] ? R0_out16 : 16'bz;  // Controlled_Buffer controlled_buffer_9
  assign {RegisterSelect_read_out8HIGH, RegisterSelect_read_out8LOW} = RegisterSelect_read_in8[1] ? R1_out16 : 16'bz;  // Controlled_Buffer controlled_buffer_10
  assign {RegisterSelect_read_out8HIGH, RegisterSelect_read_out8LOW} = RegisterSelect_read_in8[2] ? R2_out16 : 16'bz;  // Controlled_Buffer controlled_buffer_11
  assign {RegisterSelect_read_out8HIGH, RegisterSelect_read_out8LOW} = RegisterSelect_read_in8[3] ? R3_out16 : 16'bz;  // Controlled_Buffer controlled_buffer_12
  assign {RegisterSelect_read_out8HIGH, RegisterSelect_read_out8LOW} = RegisterSelect_read_in8[4] ? R4_out16 : 16'bz;  // Controlled_Buffer controlled_buffer_13
  assign {RegisterSelect_read_out8HIGH, RegisterSelect_read_out8LOW} = RegisterSelect_read_in8[5] ? R5_out16 : 16'bz;  // Controlled_Buffer controlled_buffer_14
  assign {RegisterSelect_read_out8HIGH, RegisterSelect_read_out8LOW} = RegisterSelect_read_in8[6] ? R6_out16 : 16'bz;  // Controlled_Buffer controlled_buffer_15
  assign {RegisterSelect_read_out8HIGH, RegisterSelect_read_out8LOW} = RegisterSelect_read_in8[7] ? R7_out16 : 16'bz;  // Controlled_Buffer controlled_buffer_16
  assign Register_write_in8 = and_19_out | and_20_out;  // OR_Gate or_15, 8 bits wide
  assign Register_write_in_upper8 = and_21_out | and_22_out;  // OR_Gate or_16, 8 bits wide
  or or_17 (or_17_out, segment_enable, loadToRAM);
  assign and_31_out = Reading_op2_ext8 & ALU_enable_AS8;  // AND_Gate and_31, 8 bits wide
  assign and_32_out = Rsel_ctrl_upperEnable & Rsel_ctrl_lowerEnable;  // AND_Gate and_32, 8 bits wide
  Register #(.trigger("high")) Reg0_1 (
    .D(Register_write_in8), .Q(R0_out16[7:0]), .clk(and_23_out), .clr(rst));  // open: en
  Register #(.trigger("high")) register_2 (
    .D(Register_write_in_upper8), .Q(R0_out16[15:8]), .clk(and_24_out), .clr(rst));  // open: en
  Register #(.trigger("high")) Reg1_2 (
    .D(Register_write_in8), .Q(R1_out16[7:0]), .clk(and_25_out), .clr(rst));  // open: en
  Register #(.trigger("high")) register_3 (
    .D(Register_write_in_upper8), .Q(R1_out16[15:8]), .clk(and_26_out), .clr(rst));  // open: en
  Register #(.trigger("high")) Reg2_4 (
    .D(Register_write_in8), .Q(R2_out16[7:0]), .clk(and_27_out), .clr(rst));  // open: en
  Register #(.trigger("high")) register_4 (
    .D(Register_write_in_upper8), .Q(R2_out16[15:8]), .clk(and_28_out), .clr(rst));  // open: en
  Register #(.trigger("high")) Reg3_8 (
    .D(Register_write_in8), .Q(R3_out16[7:0]), .clk(and_29_out), .clr(rst));  // open: en
  Register #(.trigger("high")) register_5 (
    .D(Register_write_in_upper8), .Q(R3_out16[15:8]), .clk(and_30_out), .clr(rst));  // open: en
  Register #(.trigger("high")) InstructionCache (
    .D(InstructionCache_input8), .Q(InstructionCache_out8), .clk(InstructionCache_write), .clr(rst));  // open: en
  Register #(.trigger("high")) Operand1Cache (
    .D(InstructionCache_input8), .Q(Operand1Cache_out8), .clk(Operand1Cache_write), .clr(rst));  // open: en
  Register #(.trigger("high"), .width(16)) Temp16Register (
    .D(Rt16_input16), .Q(Rt16_out16), .clk(Operand1Cache_write), .clr(rst));  // open: en
  Register #(.trigger("high"), .width(4)) FLAGS (
    .D(FLAGS_in4), .Q(FLAGS_out4), .clk(FLAGS_write), .clr(rst));  // open: en
  Pull_Resistor pull_resistor_2 (.node({RegisterSelect_read_out8HIGH, RegisterSelect_read_out8LOW}));
  and and_33 (ram_wrt, or_17_out, Reading_op2);
  assign {Registers_allbits, and_34_out} = and_31_out & and_32_out;  // AND_Gate and_34, 8 bits wide
  assign {Registers_highbits_req2, and_35_out} = and_31_out & Rsel_ctrl_upperEnable;  // AND_Gate and_35, 8 bits wide
  not not_14 (not_14_out, clk);
  not not_15 (not_15_out, or_18_out);
  or or_18 (or_18_out, Registers_highbits, Registers_allbits);
  not not_16 (not_16_out, or_18_out);
  not not_17 (not_17_out, or_18_out);
  not not_18 (not_18_out, or_18_out);
  assign clk_inv_as8 = {{7{not_14_out}}, not_14_out};  // Bit_Extender bit_extender_8
  Pull_Resistor pull_resistor_3 (.node(RegisterSelect_write_in8));
  assign RegisterSelect_write_in8 = and_31_out[7] ? {Operand1Cache_out8SAFE, JMP_addr[1:0]} : 8'bz;  // Controlled_Buffer controlled_buffer_17
  or or_19 (or_19_out, Registers_allbits, not_15_out);
  and and_36 (and_36_out, or_19_out, R4_write);
  and and_37 (and_37_out, R4_write, or_18_out);
  or or_20 (or_20_out, Registers_allbits, not_16_out);
  and and_38 (and_38_out, or_20_out, R5_write);
  and and_39 (and_39_out, R5_write, or_18_out);
  or or_21 (or_21_out, Registers_allbits, not_17_out);
  and and_40 (and_40_out, or_21_out, R6_write);
  and and_41 (and_41_out, R6_write, or_18_out);
  or or_22 (or_22_out, Registers_allbits, not_18_out);
  and and_42 (and_42_out, or_22_out, R7_write);
  and and_43 (and_43_out, R7_write, or_18_out);
  assign {R7_write, R6_write, R5_write, R4_write, R3_write, R2_write, R1_write, R0_write} = RegisterSelect_write_in8 & clk_inv_as8;  // AND_Gate and_44, 8 bits wide
  Register #(.trigger("high")) Reg4 (
    .D(Register_write_in8), .Q(R4_out16[7:0]), .clk(and_36_out), .clr(rst));  // open: en
  Register #(.trigger("high")) register_6 (
    .D(Register_write_in_upper8), .Q(R4_out16[15:8]), .clk(and_37_out), .clr(rst));  // open: en
  Register #(.trigger("high")) Reg5 (
    .D(Register_write_in8), .Q(R5_out16[7:0]), .clk(and_38_out), .clr(rst));  // open: en
  Register #(.trigger("high")) register_7 (
    .D(Register_write_in_upper8), .Q(R5_out16[15:8]), .clk(and_39_out), .clr(rst));  // open: en
  Register #(.trigger("high")) Reg6 (
    .D(Register_write_in8), .Q(R6_out16[7:0]), .clk(and_40_out), .clr(rst));  // open: en
  Register #(.trigger("high")) register_8 (
    .D(Register_write_in_upper8), .Q(R6_out16[15:8]), .clk(and_41_out), .clr(rst));  // open: en
  Register #(.trigger("high")) Reg7 (
    .D(Register_write_in8), .Q(R7_out16[7:0]), .clk(and_42_out), .clr(rst));  // open: en
  Register #(.trigger("high")) register_9 (
    .D(Register_write_in_upper8), .Q(R7_out16[15:8]), .clk(and_43_out), .clr(rst));  // open: en
  Register #(.trigger("high")) SegmentRegister (
    .D(ram_write_in8), .Q({Rseg_out8, Rseg_out2}), .clk(Rseg_write), .clr(rst));  // open: en
  Register #(.trigger("high")) TemporaryRegister (
    .D(Rt16_input16[7:0]), .Q(ram_write_in8), .clk(Operand1Cache_write), .clr(rst));  // open: en
  Register #(.trigger("high"), .width(2)) SelectorRegister (
    .D(2'b00), .Q(Rsel_out2), .clk(1'b1), .clr(rst));  // open: en
  all8equal_main main_1 (.in_1(8'h1), .in_2(InstructionCache_out8SAFE), .out_3(main_1_out_3));
  all8equal_main main_2 (.in_1(8'h2), .in_2(InstructionCache_out8SAFE), .out_3(main_2_out_3));
  all8equal_main main_3 (.in_1(8'h3), .in_2(InstructionCache_out8SAFE), .out_3(main_3_out_3));
  all8equal_main main_4 (.in_1(8'h4), .in_2(InstructionCache_out8SAFE), .out_3(main_4_out_3));
  all8equal_main main_5 (.in_1(8'h5), .in_2(InstructionCache_out8SAFE), .out_3(main_5_out_3));
  all8equal_main main_6 (.in_1(8'h6), .in_2(InstructionCache_out8SAFE), .out_3(main_6_out_3));
  or or_23 (FLAGS_write, FLAGS_write_cmp, IC_editIntFlag);
  or or_24 (or_24_out, main_1_out_3, main_2_out_3, main_3_out_3, main_4_out_3, main_5_out_3, main_6_out_3);
  assign FLAGS_in4 = FLAGS_write_cmp ? {FLAGS_out4[3:2], ALU_cmp_out2} : 4'bz;  // Controlled_Buffer controlled_buffer_18
  assign FLAGS_in4 = IC_editIntFlag ? {FLAGS_out4[3], IC_intWasTrig, FLAGS_out4[1:0]} : 4'bz;  // Controlled_Buffer controlled_buffer_19
  not not_19 (not_19_out, clk);
  and and_45 (and_45_out, or_24_out, not_19_out);
  assign RegisterSelect_write_in8 = and_45_out ? JMP_addr[9:2] : 8'bz;  // Controlled_Buffer controlled_buffer_20
  Demultiplexer #(.select(4)) demultiplexer_2 (
    .out1(demultiplexer_2_out1), .out2(demultiplexer_2_out2), .out3(demultiplexer_2_out3),
    .out4(demultiplexer_2_out4), .out5(demultiplexer_2_out5), .out6(demultiplexer_2_out6),
    .out7(demultiplexer_2_out7), .out8(demultiplexer_2_out8), .out9(demultiplexer_2_out9),
    .out10(demultiplexer_2_out10), .out11(demultiplexer_2_out11), .out12(demultiplexer_2_out12), .in(1'b1),
    .sel(ALU_select_in4));  // open: out0, out13, out14, out15
  not not_20 (not_20_out, clk);
  and and_46 (and_46_out, or_26_out, not_20_out);
  assign RegisterSelect_write_in8 = and_46_out ? JMP_addr[9:2] : 8'bz;  // Controlled_Buffer controlled_buffer_21
  all8equal_main main_7 (.in_1(8'h7), .in_2(InstructionCache_out8SAFE), .out_3(main_7_out_3));
  all8equal_main main_8 (.in_1(8'h8), .in_2(InstructionCache_out8SAFE), .out_3(main_8_out_3));
  all8equal_main main_9 (.in_1(8'h9), .in_2(InstructionCache_out8SAFE), .out_3(main_9_out_3));
  all8equal_main main_10 (.in_1(8'ha), .in_2(InstructionCache_out8SAFE), .out_3(main_10_out_3));
  all8equal_main main_11 (.in_1(8'hb), .in_2(InstructionCache_out8SAFE), .out_3(main_11_out_3));
  all8equal_main main_12 (.in_1(8'hc), .in_2(InstructionCache_out8SAFE), .out_3(main_12_out_3));
  Adder #(.width(16)) adder_1 (.a(ALU_inputA_in16), .b(ALU_inputB_in16), .out(adder_1_out));  // open: cin, cout
  Subtractor #(.width(16)) subtractor_1 (
    .a(ALU_inputA_in16), .b(ALU_inputB_in16), .out(subtractor_1_out));  // open: bin, bout
  Multiplier #(.width(16)) multiplier_1 (
    .a(ALU_inputA_in16), .b(ALU_inputB_in16), .out(multiplier_1_out));  // open: cin, cout
  Divider #(.width(16)) divider_1 (.a(ALU_inputA_in16), .b(ALU_inputB_in16), .out(divider_1_out));  // open: upper, rem
  Shifter #(.width(16)) shifter_1 (.in(ALU_inputA_in16), .\dist (ALU_inputB_in16[3:0]), .out(shifter_1_out));
  Shifter #(.shift("lr"), .width(16)) shifter_2 (
    .in(ALU_inputA_in16), .\dist (ALU_inputB_in16[3:0]), .out(shifter_2_out));
  Shifter #(.shift("rl"), .width(16)) shifter_3 (
    .in(ALU_inputA_in16), .\dist (ALU_inputB_in16[3:0]), .out(shifter_3_out));
  Shifter #(.shift("rl"), .width(16)) shifter_4 (
    .in(ALU_inputA_in16), .\dist (ALU_inputB_in16[3:0]), .out(shifter_4_out));
  assign or_25_out = ALU_inputA_in16 | ALU_inputB_in16;  // OR_Gate or_25, 16 bits wide
  assign and_47_out = ALU_inputA_in16 & ALU_inputB_in16;  // AND_Gate and_47, 16 bits wide
  assign xor_1_out = ALU_inputA_in16 ^ ALU_inputB_in16;  // XOR_Gate xor_1, 16 bits wide
  Comparator #(.mode("unsigned"), .width(16)) comparator_1 (
    .a(ALU_inputA_in16), .b(ALU_inputB_in16), .gt(comparator_1_gt[0]), .eq(comparator_1_gt[1]));  // open: lt
  assign {ALU_out8HIGH, ALU_out8LOW} = demultiplexer_2_out1 ? adder_1_out : 16'bz;  // Controlled_Buffer controlled_buffer_22
  assign {ALU_out8HIGH, ALU_out8LOW} = demultiplexer_2_out2 ? subtractor_1_out : 16'bz;  // Controlled_Buffer controlled_buffer_23
  assign {ALU_out8HIGH, ALU_out8LOW} = demultiplexer_2_out3 ? multiplier_1_out : 16'bz;  // Controlled_Buffer controlled_buffer_24
  assign {ALU_out8HIGH, ALU_out8LOW} = demultiplexer_2_out4 ? divider_1_out : 16'bz;  // Controlled_Buffer controlled_buffer_25
  assign {ALU_out8HIGH, ALU_out8LOW} = demultiplexer_2_out5 ? shifter_1_out : 16'bz;  // Controlled_Buffer controlled_buffer_26
  assign {ALU_out8HIGH, ALU_out8LOW} = demultiplexer_2_out6 ? shifter_2_out : 16'bz;  // Controlled_Buffer controlled_buffer_27
  assign {ALU_out8HIGH, ALU_out8LOW} = demultiplexer_2_out7 ? shifter_3_out : 16'bz;  // Controlled_Buffer controlled_buffer_28
  assign {ALU_out8HIGH, ALU_out8LOW} = demultiplexer_2_out8 ? shifter_4_out : 16'bz;  // Controlled_Buffer controlled_buffer_29
  assign {ALU_out8HIGH, ALU_out8LOW} = demultiplexer_2_out9 ? or_25_out : 16'bz;  // Controlled_Buffer controlled_buffer_30
  assign {ALU_out8HIGH, ALU_out8LOW} = demultiplexer_2_out10 ? and_47_out : 16'bz;  // Controlled_Buffer controlled_buffer_31
  assign {ALU_out8HIGH, ALU_out8LOW} = demultiplexer_2_out11 ? xor_1_out : 16'bz;  // Controlled_Buffer controlled_buffer_32
  assign ALU_cmp_out2 = demultiplexer_2_out12 ? comparator_1_gt : 2'bz;  // Controlled_Buffer controlled_buffer_33
  Pull_Resistor pull_resistor_4 (.node({ALU_out8HIGH, ALU_out8LOW}));
  or or_26 (or_26_out, main_7_out_3, main_8_out_3, main_9_out_3, main_10_out_3, main_11_out_3, main_12_out_3);
  or or_27 (or_27_out, main_13_out_3, main_14_out_3, main_15_out_3, main_16_out_3, main_17_out_3, 1'b0);
  or or_28 (Registers_highbits_req1, or_26_out, or_27_out);
  all8equal_main main_13 (.in_1(InstructionCache_out8LOCK1), .in_2(8'h6), .out_3(main_13_out_3));
  all8equal_main main_14 (.in_1(InstructionCache_out8LOCK1), .in_2(8'hb), .out_3(main_14_out_3));
  all8equal_main main_15 (.in_1(InstructionCache_out8LOCK1), .in_2(8'hf), .out_3(main_15_out_3));
  all8equal_main main_16 (.in_1(InstructionCache_out8LOCK1), .in_2(8'h16), .out_3(main_16_out_3));
  all8equal_main main_17 (.in_1(InstructionCache_out8LOCK1), .in_2(8'h17), .out_3(main_17_out_3));
  Pull_Resistor pull_resistor_5 (.node(ALU_cmp_out2));
  all8equal_main main_18 (.in_1(8'h3), .in_2(InstructionCache_out8LOCK1), .out_3(main_18_out_3));
  all8equal_main main_19 (.in_1(8'h9), .in_2(InstructionCache_out8LOCK1), .out_3(main_19_out_3));
  all8equal_main main_20 (.in_1(8'h11), .in_2(InstructionCache_out8LOCK1));  // open: out_3
  all8equal_main main_21 (.in_2(InstructionCache_out8LOCK1));  // open: in_1, out_3
  all8equal_main main_22 (.in_2(InstructionCache_out8LOCK1));  // open: in_1, out_3
  all8equal_main main_23 (.in_2(InstructionCache_out8LOCK1));  // open: in_1, out_3
  or or_29 (or_29_out, main_18_out_3, main_19_out_3, 1'b0, 1'b0, 1'b0, 1'b0);
  or or_30 (or_30_out, main_48_out_3, main_49_out_3, main_50_out_3, 1'b0, 1'b0, 1'b0);
  or or_31 (segment_enable, or_29_out, or_30_out);
  assign bit_extender_9_out = {{8{1'b0}}, JMP_addr[9:2]};  // Bit_Extender bit_extender_9
  all8equal_main main_24 (.in_1(InstructionCache_out8SAFE), .in_2(8'h18), .out_3(main_24_out_3));
  all8equal_main main_25 (.in_1(InstructionCache_out8SAFE), .in_2(8'h1c), .out_3(main_25_out_3));
  all8equal_main main_26 (.in_1(InstructionCache_out8SAFE), .in_2(8'h19), .out_3(main_26_out_3));
  all8equal_main main_27 (.in_1(InstructionCache_out8SAFE), .in_2(8'h1d), .out_3(main_27_out_3));
  all8equal_main main_28 (.in_1(InstructionCache_out8SAFE), .in_2(8'h1a), .out_3(main_28_out_3));
  all8equal_main main_29 (.in_1(InstructionCache_out8SAFE), .in_2(8'h1e), .out_3(main_29_out_3));
  all8equal_main main_30 (.in_1(InstructionCache_out8SAFE), .in_2(8'h1b), .out_3(main_30_out_3));
  all8equal_main main_31 (.in_1(InstructionCache_out8SAFE), .in_2(8'h1f), .out_3(main_31_out_3));
  all8equal_main main_32 (.in_1(InstructionCache_out8SAFE), .in_2(8'h26), .out_3(main_32_out_3));
  all8equal_main main_33 (.in_1(InstructionCache_out8SAFE), .in_2(8'h2e), .out_3(main_33_out_3));
  all8equal_main main_34 (.in_1(InstructionCache_out8SAFE), .in_2(8'h27), .out_3(main_34_out_3));
  all8equal_main main_35 (.in_1(InstructionCache_out8SAFE), .in_2(8'h2f), .out_3(main_35_out_3));
  all8equal_main main_36 (.in_1(InstructionCache_out8SAFE), .in_2(8'h28), .out_3(main_36_out_3));
  all8equal_main main_37 (.in_1(InstructionCache_out8SAFE), .in_2(8'h30), .out_3(main_37_out_3));
  all8equal_main main_38 (.in_1(InstructionCache_out8SAFE), .in_2(8'h29), .out_3(main_38_out_3));
  all8equal_main main_39 (.in_1(InstructionCache_out8SAFE), .in_2(8'h31), .out_3(main_39_out_3));
  all8equal_main main_40 (.in_1(InstructionCache_out8SAFE), .in_2(8'h2a), .out_3(main_40_out_3));
  all8equal_main main_41 (.in_1(InstructionCache_out8SAFE), .in_2(8'h32), .out_3(main_41_out_3));
  all8equal_main main_42 (.in_1(InstructionCache_out8SAFE), .in_2(8'h2b), .out_3(main_42_out_3));
  all8equal_main main_43 (.in_1(InstructionCache_out8SAFE), .in_2(8'h33), .out_3(main_43_out_3));
  all8equal_main main_44 (.in_1(InstructionCache_out8SAFE), .in_2(8'h2c), .out_3(main_44_out_3));
  all8equal_main main_45 (.in_1(InstructionCache_out8SAFE), .in_2(8'h34), .out_3(main_45_out_3));
  all8equal_main main_46 (.in_1(InstructionCache_out8SAFE), .in_2(8'h2d), .out_3(main_46_out_3));
  all8equal_main main_47 (.in_1(InstructionCache_out8SAFE), .in_2(8'h35), .out_3(main_47_out_3));
  assign and_48_out = {RegisterSelect_read_out8HIGH, RegisterSelect_read_out8LOW} & {registerReadFromOp2_AS16, registerReadFromOp2_AS8};  // AND_Gate and_48, 16 bits wide
  or or_32 (or_32_out, main_24_out_3, main_25_out_3);
  or or_33 (or_33_out, main_26_out_3, main_27_out_3);
  or or_34 (or_34_out, main_28_out_3, main_29_out_3);
  or or_35 (or_35_out, main_30_out_3, main_31_out_3);
  or or_36 (or_36_out, main_32_out_3, main_33_out_3);
  or or_37 (or_37_out, main_34_out_3, main_35_out_3);
  or or_38 (or_38_out, main_36_out_3, main_37_out_3);
  or or_39 (or_39_out, main_38_out_3, main_39_out_3);
  or or_40 (or_40_out, main_40_out_3, main_41_out_3);
  or or_41 (or_41_out, main_42_out_3, main_43_out_3);
  or or_42 (or_42_out, main_44_out_3, main_45_out_3);
  or or_43 (or_43_out, main_46_out_3, main_47_out_3);
  all8equal_main main_48 (.in_1(InstructionCache_out8SAFE), .in_2(8'h13), .out_3(main_48_out_3));
  all8equal_main main_49 (.in_1(InstructionCache_out8SAFE), .in_2(8'h15), .out_3(main_49_out_3));
  all8equal_main main_50 (.in_1(InstructionCache_out8SAFE), .in_2(8'h17), .out_3(main_50_out_3));
  assign segment_enable_AS8 = {{7{segment_enable}}, segment_enable};  // Bit_Extender bit_extender_10
  assign ALU_select_in4 = or_32_out ? 4'b1001 : 4'bz;  // Controlled_Buffer controlled_buffer_34
  assign ALU_select_in4 = or_33_out ? 4'b1010 : 4'bz;  // Controlled_Buffer controlled_buffer_35
  assign ALU_select_in4 = or_34_out ? 4'b1011 : 4'bz;  // Controlled_Buffer controlled_buffer_36
  assign ALU_select_in4 = or_35_out ? 4'b1100 : 4'bz;  // Controlled_Buffer controlled_buffer_37
  assign ALU_select_in4 = or_36_out ? 4'b0001 : 4'bz;  // Controlled_Buffer controlled_buffer_38
  assign ALU_select_in4 = or_37_out ? 4'b0010 : 4'bz;  // Controlled_Buffer controlled_buffer_39
  assign ALU_select_in4 = or_38_out ? 4'b0011 : 4'bz;  // Controlled_Buffer controlled_buffer_40
  assign ALU_select_in4 = or_39_out ? 4'b0100 : 4'bz;  // Controlled_Buffer controlled_buffer_41
  assign ALU_select_in4 = or_40_out ? 4'b0101 : 4'bz;  // Controlled_Buffer controlled_buffer_42
  assign ALU_select_in4 = or_41_out ? 4'b0110 : 4'bz;  // Controlled_Buffer controlled_buffer_43
  assign ALU_select_in4 = or_42_out ? 4'b0111 : 4'bz;  // Controlled_Buffer controlled_buffer_44
  assign ALU_select_in4 = or_43_out ? 4'b1000 : 4'bz;  // Controlled_Buffer controlled_buffer_45
  assign {or_44_out_2, or_44_out} = and_48_out | {16{1'b0}};  // OR_Gate or_44, 16 bits wide
  Pull_Resistor pull_resistor_6 (.node(ALU_select_in4));
  assign ALU_inputA_in16[7:0] = Rsel_ctrl_lowerEnable & Rt16_out16[7:0];  // AND_Gate and_49, 8 bits wide
  assign ALU_inputA_in16[15:8] = Rt16_out16[15:8] & Rsel_ctrl_upperEnable;  // AND_Gate and_50, 8 bits wide
  all8equal_main main_51 (.in_1(or_44_out), .in_2({8{1'b0}}), .out_3(main_51_out_3));
  all8equal_main main_52 (.in_1(or_44_out_2), .in_2({8{1'b0}}), .out_3(main_52_out_3));
  and and_51 (and_51_out, main_51_out_3, main_52_out_3);
  not not_21 (not_21_out, and_51_out);
  assign controlled_buffer_46_out = and_51_out ? bit_extender_9_out : 16'bz;  // Controlled_Buffer controlled_buffer_46
  assign controlled_buffer_46_out = not_21_out ? {or_44_out_2, or_44_out} : 16'bz;  // Controlled_Buffer controlled_buffer_47
  or or_45 (or_45_out, Rsel_out2[0], Rsel_out2[1]);
  not not_22 (not_22_out, Rsel_out2[0]);
  assign bit_extender_11_out = {{4{1'b0}}, ALU_select_in4};  // Bit_Extender bit_extender_11
  all8equal_main main_53 (.in_1(8'hd), .in_2(InstructionCache_out8SAFE), .out_3(main_53_out_3));
  all8equal_main main_54 (.in_1(8'he), .in_2(InstructionCache_out8SAFE), .out_3(main_54_out_3));
  all8equal_main main_55 (.in_1(8'hf), .in_2(InstructionCache_out8SAFE), .out_3(main_55_out_3));
  all8equal_main main_56 (.in_1(8'h10), .in_2(InstructionCache_out8SAFE), .out_3(main_56_out_3));
  all8equal_main main_57 (.in_1(8'h11), .in_2(InstructionCache_out8SAFE), .out_3(main_57_out_3));
  assign Rsel_ctrl_upperEnable = {{7{or_45_out}}, or_45_out};  // Bit_Extender bit_extender_12
  or or_46 (or_46_out, not_22_out, Rsel_out2[1]);
  all8equal_main main_58 (.in_1(bit_extender_11_out), .in_2({8{1'b0}}), .out_3(main_58_out_3));
  or or_47 (Rseg_write, main_53_out_3, main_54_out_3, main_55_out_3, main_56_out_3, main_57_out_3);
  assign Rsel_ctrl_lowerEnable = {{7{or_46_out}}, or_46_out};  // Bit_Extender bit_extender_13
  assign ALU_enable_AS8 = {{7{not_23_out}}, not_23_out};  // Bit_Extender bit_extender_14
  not not_23 (not_23_out, main_58_out_3);
  assign ALU_inputB_in16[7:0] = Rsel_ctrl_lowerEnable & controlled_buffer_46_out[7:0];  // AND_Gate and_52, 8 bits wide
  assign ALU_inputB_in16[15:8] = controlled_buffer_46_out[15:8] & Rsel_ctrl_upperEnable;  // AND_Gate and_53, 8 bits wide
  all8equal_main main_59 (.in_1(8'h2), .in_2(InstructionCache_out8LOCK1), .out_3(main_59_out_3));
  all8equal_main main_60 (.in_1(8'h8), .in_2(InstructionCache_out8LOCK1), .out_3(main_60_out_3));
  all8equal_main main_61 (.in_1(8'h10), .in_2(InstructionCache_out8LOCK1), .out_3(main_61_out_3));
  all8equal_main main_62 (.in_1(undriven_4), .in_2(InstructionCache_out8LOCK1));  // open: out_3
  all8equal_main main_63 (.in_1(undriven_5), .in_2(InstructionCache_out8LOCK1));  // open: out_3
  or or_48 (Rtemp_loadFromRAM, main_59_out_3, main_60_out_3, main_61_out_3, 1'b0, 1'b0);
  assign Rtemp_loadFromRAM_AS8 = {{7{Rtemp_loadFromRAM}}, Rtemp_loadFromRAM};  // Bit_Extender bit_extender_15
  all8equal_main main_64 (.in_1(8'h5), .in_2(InstructionCache_out8LOCK1), .out_3(main_64_out_3));
  all8equal_main main_65 (.in_1(8'h6), .in_2(InstructionCache_out8LOCK1), .out_3(main_65_out_3));
  all8equal_main main_66 (.in_1(8'hb), .in_2(InstructionCache_out8LOCK1), .out_3(main_66_out_3));
  all8equal_main main_67 (.in_1(8'hc), .in_2(InstructionCache_out8LOCK1), .out_3(main_67_out_3));
  all8equal_main main_68 (.in_1(8'he), .in_2(InstructionCache_out8LOCK1), .out_3(main_68_out_3));
  all8equal_main main_69 (.in_1(8'hf), .in_2(InstructionCache_out8LOCK1), .out_3(main_69_out_3));
  all8equal_main main_70 (.in_1(8'h14), .in_2(InstructionCache_out8LOCK1), .out_3(main_70_out_3));
  all8equal_main main_71 (.in_1(8'h15), .in_2(InstructionCache_out8LOCK1), .out_3(main_71_out_3));
  all8equal_main main_72 (.in_1(8'h16), .in_2(InstructionCache_out8LOCK1), .out_3(main_72_out_3));
  all8equal_main main_73 (.in_1(8'h17), .in_2(InstructionCache_out8LOCK1), .out_3(main_73_out_3));
  all8equal_main main_74 (.in_1(8'h18), .in_2(InstructionCache_out8LOCK1), .out_3(main_74_out_3));
  all8equal_main main_75 (.in_1(8'h19), .in_2(InstructionCache_out8LOCK1), .out_3(main_75_out_3));
  all8equal_main main_76 (.in_1(8'h1a), .in_2(InstructionCache_out8LOCK1), .out_3(main_76_out_3));
  all8equal_main main_77 (.in_1(8'h1b), .in_2(InstructionCache_out8LOCK1), .out_3(main_77_out_3));
  all8equal_main main_78 (.in_1(8'h1c), .in_2(InstructionCache_out8LOCK1), .out_3(main_78_out_3));
  all8equal_main main_79 (.in_1(8'h1d), .in_2(InstructionCache_out8LOCK1), .out_3(main_79_out_3));
  all8equal_main main_80 (.in_1(8'h1e), .in_2(InstructionCache_out8LOCK1), .out_3(main_80_out_3));
  all8equal_main main_81 (.in_1(8'h1f), .in_2(InstructionCache_out8LOCK1), .out_3(main_81_out_3));
  all8equal_main main_82 (.in_1(8'h26), .in_2(InstructionCache_out8LOCK1), .out_3(main_82_out_3));
  all8equal_main main_83 (.in_1(8'h27), .in_2(InstructionCache_out8LOCK1), .out_3(main_83_out_3));
  all8equal_main main_84 (.in_1(8'h28), .in_2(InstructionCache_out8LOCK1), .out_3(main_84_out_3));
  all8equal_main main_85 (.in_1(8'h29), .in_2(InstructionCache_out8LOCK1), .out_3(main_85_out_3));
  all8equal_main main_86 (.in_1(8'h2a), .in_2(InstructionCache_out8LOCK1), .out_3(main_86_out_3));
  all8equal_main main_87 (.in_1(8'h2b), .in_2(InstructionCache_out8LOCK1), .out_3(main_87_out_3));
  all8equal_main main_88 (.in_1(8'h2c), .in_2(InstructionCache_out8LOCK1), .out_3(main_88_out_3));
  all8equal_main main_89 (.in_1(8'h2d), .in_2(InstructionCache_out8LOCK1), .out_3(main_89_out_3));
  all8equal_main main_90 (.in_1(8'h2e), .in_2(InstructionCache_out8LOCK1), .out_3(main_90_out_3));
  all8equal_main main_91 (.in_1(8'h2f), .in_2(InstructionCache_out8LOCK1), .out_3(main_91_out_3));
  all8equal_main main_92 (.in_1(8'h30), .in_2(InstructionCache_out8LOCK1), .out_3(main_92_out_3));
  all8equal_main main_93 (.in_1(8'h31), .in_2(InstructionCache_out8LOCK1), .out_3(main_93_out_3));
  all8equal_main main_94 (.in_1(8'h32), .in_2(InstructionCache_out8LOCK1), .out_3(main_94_out_3));
  all8equal_main main_95 (.in_1(8'h33), .in_2(InstructionCache_out8LOCK1), .out_3(main_95_out_3));
  all8equal_main main_96 (.in_1(8'h34), .in_2(InstructionCache_out8LOCK1), .out_3(main_96_out_3));
  all8equal_main main_97 (.in_1(8'h35), .in_2(InstructionCache_out8LOCK1), .out_3(main_97_out_3));
  or or_49 (or_49_out, main_64_out_3, main_65_out_3, main_66_out_3, main_67_out_3, main_68_out_3, main_69_out_3, main_70_out_3, main_71_out_3, main_72_out_3, main_73_out_3, main_74_out_3, main_75_out_3, main_76_out_3, main_77_out_3, main_78_out_3, main_79_out_3, main_80_out_3, main_81_out_3);
  or or_50 (or_50_out, main_82_out_3, main_83_out_3, main_84_out_3, main_85_out_3, main_86_out_3, main_87_out_3, main_88_out_3, main_89_out_3, main_90_out_3, main_91_out_3, main_92_out_3, main_93_out_3, main_94_out_3, main_95_out_3, main_96_out_3, main_97_out_3, 1'b0, 1'b0);
  or or_51 (Rtemp_loadFromREG, or_49_out, or_50_out);
  assign Rtemp_loadFromREG_AS8 = {{7{Rtemp_loadFromREG}}, Rtemp_loadFromREG};  // Bit_Extender bit_extender_16
  all8equal_main main_98 (.in_1(8'h4), .in_2(InstructionCache_out8LOCK1), .out_3(main_98_out_3));
  all8equal_main main_99 (.in_1(8'ha), .in_2(InstructionCache_out8LOCK1), .out_3(main_99_out_3));
  all8equal_main main_100 (.in_1(undriven_6), .in_2(InstructionCache_out8LOCK1));  // open: out_3
  all8equal_main main_101 (.in_1(undriven_7), .in_2(InstructionCache_out8LOCK1));  // open: out_3
  all8equal_main main_102 (.in_1(undriven_8), .in_2(InstructionCache_out8LOCK1));  // open: out_3
  or or_52 (or_52_out, main_98_out_3, main_99_out_3, 1'b0, 1'b0, 1'b0);
  assign Rtemp_loadFromSEG_AS8 = {{7{or_52_out}}, or_52_out};  // Bit_Extender bit_extender_17
  all8equal_main main_103 (.in_1(8'h12), .in_2(InstructionCache_out8SAFE), .out_3(main_103_out_3));
  all8equal_main main_104 (.in_1(8'h14), .in_2(InstructionCache_out8SAFE), .out_3(main_104_out_3));
  all8equal_main main_105 (.in_1(8'h16), .in_2(InstructionCache_out8SAFE), .out_3(main_105_out_3));
  all8equal_main main_106 (.in_1(undriven_9), .in_2(InstructionCache_out8SAFE));  // open: out_3
  all8equal_main main_107 (.in_1(undriven_10), .in_2(InstructionCache_out8SAFE));  // open: out_3
  or or_53 (loadToRAM, main_103_out_3, main_104_out_3, main_105_out_3, 1'b0, 1'b0);
  assign loadToMem_AS8 = {{7{loadToRAM}}, loadToRAM};  // Bit_Extender bit_extender_18
  all8equal_main main_108 (.in_1(8'h1c), .in_2(InstructionCache_out8SAFE), .out_3(main_108_out_3));
  all8equal_main main_109 (.in_1(8'h1d), .in_2(InstructionCache_out8SAFE), .out_3(main_109_out_3));
  all8equal_main main_110 (.in_1(8'h1e), .in_2(InstructionCache_out8SAFE), .out_3(main_110_out_3));
  all8equal_main main_111 (.in_1(8'h1f), .in_2(InstructionCache_out8SAFE), .out_3(main_111_out_3));
  all8equal_main main_112 (.in_1(8'h2e), .in_2(InstructionCache_out8SAFE), .out_3(main_112_out_3));
  all8equal_main main_113 (.in_1(8'h2f), .in_2(InstructionCache_out8SAFE), .out_3(main_113_out_3));
  all8equal_main main_114 (.in_1(8'h30), .in_2(InstructionCache_out8SAFE), .out_3(main_114_out_3));
  all8equal_main main_115 (.in_1(8'h31), .in_2(InstructionCache_out8SAFE), .out_3(main_115_out_3));
  all8equal_main main_116 (.in_1(8'h32), .in_2(InstructionCache_out8SAFE), .out_3(main_116_out_3));
  all8equal_main main_117 (.in_1(8'h33), .in_2(InstructionCache_out8SAFE), .out_3(main_117_out_3));
  all8equal_main main_118 (.in_1(8'h34), .in_2(InstructionCache_out8SAFE), .out_3(main_118_out_3));
  all8equal_main main_119 (.in_1(8'h35), .in_2(InstructionCache_out8SAFE), .out_3(main_119_out_3));
  or or_54 (or_54_out, main_108_out_3, main_109_out_3, main_110_out_3, main_111_out_3, main_112_out_3);
  or or_55 (or_55_out, or_54_out, or_56_out);
  or or_56 (or_56_out, main_113_out_3, main_114_out_3, main_115_out_3, main_116_out_3, main_117_out_3, main_118_out_3, main_119_out_3);
  assign {registerReadFromOp2_AS16, registerReadFromOp2_AS8} = {{15{or_55_out}}, or_55_out};  // Bit_Extender bit_extender_19
  all8equal_main main_120 (.in_1(8'h1b), .in_2(InstructionCache_out8SAFE), .out_3(main_120_out_3));
  all8equal_main main_121 (.in_1(8'h1f), .in_2(InstructionCache_out8SAFE), .out_3(main_121_out_3));
  all8equal_main main_122 (.in_1(undriven_11), .in_2(InstructionCache_out8SAFE), .out_3(main_122_out_3));
  all8equal_main main_123 (.in_1(undriven_12), .in_2(InstructionCache_out8SAFE), .out_3(main_123_out_3));
  all8equal_main main_124 (.in_1(undriven_13), .in_2(InstructionCache_out8SAFE));  // open: out_3
  or or_57 (FLAGS_write_cmp, main_120_out_3, main_121_out_3, 1'b0, 1'b0, 1'b0);
  all8equal_main main_125 (.in_1(8'h36), .in_2(InstructionCache_out8SAFE), .out_3(main_125_out_3));
  all8equal_main main_126 (.in_1(undriven_14), .in_2(InstructionCache_out8SAFE));  // open: out_3
  all8equal_main main_127 (.in_1(undriven_15), .in_2(InstructionCache_out8SAFE), .out_3(main_127_out_3));
  all8equal_main main_128 (.in_1(undriven_16), .in_2(InstructionCache_out8SAFE), .out_3(main_128_out_3));
  all8equal_main main_129 (.in_1(undriven_17), .in_2(InstructionCache_out8SAFE));  // open: out_3
  or or_58 (JMP_enable, main_125_out_3, 1'b0, 1'b0, 1'b0, 1'b0);

  // Other names for the same wires on the sheet: ALU_out16[15:0] = {ALU_out8HIGH, ALU_out8LOW};
  //   FLAGS_write_req1 = FLAGS_write_cmp; InterruptMask_out8[1:0] = {InterruptMask_has2, InterruptMask_has1};
  //   Operand1Cache_out8SAFE[1:0] = JMP_addr[1:0]; Operand2[7:0] = JMP_addr[9:2];
  //   memout[7:0] = InstructionCache_input8; Operand1Cache_input8[7:0] = InstructionCache_input8;
  //   ram_addr_in10[7:0] = ram_addr_in8; Rseg_input8[7:0] = ram_write_in8; Rtemp_out8[7:0] = ram_write_in8;
  //   Reading_instruction = InstructionCache_write; registerReadFromOp2_AS16[7:0] = registerReadFromOp2_AS8;
  //   RegisterSelect_read_out16[15:0] = {RegisterSelect_read_out8HIGH, RegisterSelect_read_out8LOW};
  //   Rseg_out8[1:0] = Rseg_out2; Rtemp_input8[7:0] = Rt16_input16[7:0]; Reading_op1 = Operand1Cache_write;
  //   Rt16_write = Operand1Cache_write; Rtemp_write = Operand1Cache_write

  // Notes on the sheet:
  //   Next ins
  //   1: Code. 0: Exec
  //   Reset
  //   Instructions
  //   MAKE SURE CLK IS 0 at End of Program
  //   mem: memory offset
  //   seg: segment reg
  //   rl/rh: reg low/high
  //   Program Memory
  //   loc: memory + segment
  //   RAM -> temp
  //   Reg -> temp
  //   seg -> temp
  //   immediate-> temp
  //   Memory Addressor
  //   DATA RAM
  //   Memory is always addressed by op1 or op2
  //   implies loadFromRam
  //   Programming Switches
  //   _out8SAFE is only non-zero when currently on operand 2
  //   _out8LOCK1 is only non-zero when currently on operand 1
  //   ASX is 1 bit extended to X bits
  //   Temporary Register loader / Input Selector
  //   8 = least sig
  //   Address type selector
  //   Note that either is zeroed if not on that op
  //   If op1 requests reg read
  //   If op2 requests reg read (inverted ins)
  //   These are all off if not on operand 2
  //   Interrupt Controller
  //   Instruction
  //   Operand 1
  //   Operand 2 
  //   todo: other requests for reading here
  //   If no register or mem, use imm8
  //   ALL WRITES SHOULD BE DONE ON CLOCK LOW
  //   Operand 1: only on when on op1
  //   Cache Controller
  //   Segment combiner
  //   Highbit selector
  //   Extends input to 16 bits. Fills with 0 if not requesting register. Otherwise reads highbits
  //   Operand 1 LOCK
  //   delete
  //   todo, these should all be and'ed with clock high to prevent timing errors
  //   If ALU, feed alu instead of temp
  //   using high math, on op2, and ALU is on
  //   Operand 2 Executor
  //   It will only actually write if write command is non-zero, so only when ins requested
  //   Registers
  //   todo: set register select
  //   todo, why restricting segment to 2 bits? make it more!
  //   Enable register writing on low bits
  //   todo, if interrupt enables during cmp
  //   chip returns 1 if both entries are identical
  //   Enable register writing on high bits
  //   ALU
  //   Instruction Decoder. Todo: rework so that each instruction enables different flags instead of this mess. This was originally for visualization reasons
  //   Enable register reading on high bits
  //   todo: chain shift with higher bits on splitter
  //   reg
  //   memory (todo)
  //   imm
  //   reading
  //   ALU Input Selector
  //   Enable memory segments
  //   writing
  //   ALU Decoder
  //   Enable segment writing
  //   0: 8low 1: 8high 2: 16full
  //   Enable memory read (DO NOT INCLUDE ANY THAT READ FROM SEG)
  //   Enable register read
  //   Reads from op1
  //   Enable segment reading
  //   Enable memory writing (DO NOT INCLUDE ANY THAT WRITE FROM SEG)
  //   Enable inverted register read
  //   Reads from op2
  //   Enable FLAGS write
  //   Reads from op2
  //   Enable uncond. jump
  //   Reads from op2
endmodule
